# Fritzing sketch schematic (saved by Fritzing 0.9.3b)
circuit board: 8.46667cm x 5.64444cm
breadboards: 1

parts:
  Part1 = Arduino Uno (Rev3)
  J1 = Basic Servo
  J2 = Basic Servo
  M1 = RioRand LM2596
  VCC1 = Battery block 9V
  VCC2 = Battery block 9V
  Part2 = Bluetooth HC-05 Macho
  R1 = Resistor [tolerance=±5% resistance=220 package="2010 [SMD]"]
  S2 = Pushbutton [package="[THT]"]
  R2 = Resistor [tolerance=±5% resistance=220 package="2010 [SMD]"]

nets:
  N1: Part1.D9_PWM, J1.pulse
  N2: Part1.D10_PWM/SS, J2.pulse
  N3: Part1.D11_PWM/MOSI, Part2.RXD
  N4: Part1.D12/MISO, Part2.TXD
  GND: Part1.GND, J1.gnd, J2.gnd, M1.Pin_4, Part2.GND, R1.Pin_1, R2.Pin_0
  N5: Part1.D2, S2.Pin_1, S2.Pin_2, R2.Pin_1
  5V: Part1.5V, Part2.VCC
  N6: Part1.VIN, VCC2.+
  VCC: J1.vcc, J2.vcc, M1.Pin_3, R1.Pin_0, S2.Pin_3, S2.Pin_4
  N7: M1.Pin_1, VCC2.-
  N8: M1.Pin_2, VCC1.+

// code stored in the sketch: test.ino
#include <SoftwareSerial.h>
#include <Servo.h>
SoftwareSerial BTserial(10, 11); // RX | TX
Servo ser1;
Servo ser2;
void setup() {
  Serial.begin(38400);
  BTserial.begin(9600); 
  ser1.attach(9);
  ser2.attach(8);
}

void loop() {

  String message = "";
  if(BTserial.available()>0){
    message = BTserial.read();
    Serial.println(message);
    char c[9];
    message.toCharArray(c, 9);
    int pos1 = 0, pos2 = 0;
    pos1 = strToInt(c, 0);
    for(int i = 0; c[i]!=';'; i++){
      if(c[i] == ','){
        pos2 = strToInt(c, i+1);
      }
    }
    ser1.write(pos1);
    ser2.write(pos2);
  }
  if(Serial.available()>0){
    BTserial.println(Serial.read());
  }
  delay(20);
}

int strToInt(char c[], int pos){
  char temp[3];
  for(int i = pos, k = 0; c[i]!=';' || c[i]!=','; i++){
    if(c[i]>'0' && c[i]<'9'){
      temp[k] = c[i];
      k++;
    }else return 0;
  }
  return atoi(c);
}
